// Logisim project pipelined.circ as structural Verilog: 9 circuits, main circuit main
module ALU_control (
  input  [1:0] ALUop,
  input  [5:0] Funct,
  input  [2:0] IMM_OP,
  output [3:0] Output
);

  // PLA #(.in_width(11), .out_width(4), .truth_table("00xxxxxxxxx,0010#lw/sw\n01xxxxxxxxx,0110#beq/bne\n10xxx100001,0010#addu\n10xxx100011,0110#subu\n10xxx100100,0000#AND\n10xxx100101,0001#OR\n10xxx100111,1100#nor\n10xxx101010,0111#slt\n11001xxxxxx,0010#addiu\n11010xxxxxx,0111#slti\n11100xxxxxx,0000#andi\n11101xxxxxx,0001#ori\n10xxx000010,0010#jr\n10xxx000011,0010#jral")) pla_1: pin names not known; wires that end beside it: Output
endmodule

module Bit_extender (
  input  [15:0] Input,
  input  Signed,
  output [31:0] Output
);

  wire and_1_out;

  Multiplexer #(.width(16)) multiplexer_1 (.in0({16{1'b0}}), .in1({16{1'b1}}), .out(Output[31:16]), .sel(and_1_out));
  and and_1 (and_1_out, Input[15], Signed);

  assign Output[15:0] = Input;
endmodule

module main (
  output [1:0] out_1,
  output [1:0] out_2
);

  wire and_1_out, clock_1_out, control_1_signedimm, ex_mem_1_registerwriting_2, ex_mem_1_zero_2,
       hazard_detection_unit_1_stall, mem_wb_1_branching_2, mem_wb_1_memory_2, mips_alu_1_p4,
       mipsprogramrom_1_p4, not_1_out, or_1_out, xor_1_out;
  wire [1:0] control_1_registerwriting, id_ex_1_registerwriting_2;
  wire [2:0] control_1_alu, control_1_memory, ex_mem_1_memory_2, id_ex_1_alu_2, id_ex_1_memory_2,
       id_ex_1_op_2;
  wire [3:0] control_1_branching, ex_mem_1_branching_2, id_ex_1_branch_2, mips_alu_1_p3;
  wire [4:0] ex_mem_1_registerrd_2, ex_mem_1_registerrt_2, id_ex_1_registerrs_2, id_ex_1_registerrt_2,
       multiplexer_5_out, registerfile_1_p2;
  wire [5:0] id_ex_1_op_2_3;
  wire [27:0] id_ex_1_pc_2;
  wire [31:0] adder_1_out, adder_2_out, adder_3_out, bit_extender_1_output, ex_mem_1_branchpc_2,
       ex_mem_1_jalpc_2, ex_mem_1_jumppc_2, ex_mem_1_result_2, ex_mem_1_writedata_2, id_ex_1_data1_2,
       id_ex_1_data2_2, id_ex_1_imm_2, IF_ID_OP_q, IF_ID_PC_q, mem_wb_1_aluresult_2, mem_wb_1_memoryresult_2,
       mips_alu_1_p5, mips_ram_1_p7, mipsprogramrom_1_p2, multiplexer_1_out, multiplexer_2_out,
       multiplexer_3_out, multiplexer_4_out, multiplexer_6_out, multiplexer_8_out, PC_q, registerfile_1_p1,
       registerfile_1_p5, registerfile_1_p6, shifter_1_out;
  wire [31:8] id_ex_1_op_2_4;
  wire [31:29] id_ex_1_op_2_2;

  Multiplexer #(.width(32)) multiplexer_1 (
    .in0(adder_1_out), .in1(multiplexer_6_out), .out(multiplexer_1_out), .sel(and_1_out));
  Adder #(.width(32)) adder_1 (.a(32'h4), .b(PC_q), .out(adder_1_out));  // open: cin, cout
  Register #(.width(32)) PC (.D(multiplexer_1_out), .en(1'b1), .Q(PC_q), .clk(clock_1_out));  // open: clr
  Clock clock_1 (.out(clock_1_out));
  // MIPSProgramROM mipsprogramrom_1: pin names not known; wires that end beside it: PC_q, mipsprogramrom_1_p2, clock_1_out, mipsprogramrom_1_p4
  Register #(.width(32)) IF_ID_PC (.D(adder_1_out), .en(1'b1), .Q(IF_ID_PC_q), .clk(clock_1_out));  // open: clr
  Register #(.width(32)) IF_ID_OP (.D(mipsprogramrom_1_p2), .en(1'b1), .Q(IF_ID_OP_q), .clk(clock_1_out));  // open: clr
  // RegisterFile #(.trigger("falling")) registerfile_1: pin names not known; wires that end beside it: registerfile_1_p1, registerfile_1_p2, IF_ID_OP_q[20:16], IF_ID_OP_q[25:21], registerfile_1_p5, registerfile_1_p6
  Bit_extender bit_extender_1 (.Input(IF_ID_OP_q[15:0]), .Signed(control_1_signedimm), .Output(bit_extender_1_output));
  Control control_1 (
    .OP(IF_ID_OP_q[31:26]), .Funct(IF_ID_OP_q[5:0]), .SignedIMM(control_1_signedimm), .Alu(control_1_alu),
    .Branching(control_1_branching), .Memory(control_1_memory), .RegisterWriting(control_1_registerwriting));
  ID_EX id_ex_1 (
    .PC(IF_ID_PC_q), .Data1(registerfile_1_p5), .Data2(registerfile_1_p6), .IMM(bit_extender_1_output),
    .ALU(control_1_alu), .Branch(control_1_branching), .OP(IF_ID_OP_q), .Memory(control_1_memory),
    .RegisterWriting(control_1_registerwriting), .RegisterRs(IF_ID_OP_q[20:16]),
    .RegisterRt(IF_ID_OP_q[25:21]), .NOP(hazard_detection_unit_1_stall), .Clock(clock_1_out),
    .PC_2({id_ex_1_op_2_4[31:28], id_ex_1_pc_2}), .Data1_2(id_ex_1_data1_2), .Data2_2(id_ex_1_data2_2),
    .IMM_2(id_ex_1_imm_2), .ALU_2(id_ex_1_alu_2), .Branch_2(id_ex_1_branch_2),
    .OP_2({id_ex_1_op_2_2, id_ex_1_op_2, id_ex_1_op_2_4[27:8], id_ex_1_op_2_3}), .Memory_2(id_ex_1_memory_2),
    .RegisterWriting_2(id_ex_1_registerwriting_2), .RegisterRs_2(id_ex_1_registerrs_2),
    .RegisterRt_2(id_ex_1_registerrt_2));
  Hazard_detection_unit hazard_detection_unit_1 (
    .ID_EX_MemRead(id_ex_1_memory_2[0]), .ID_EX_RegisterRt(id_ex_1_registerrt_2),
    .IF_ID_RegisterRs(IF_ID_OP_q[20:16]), .IF_ID_RegisterRt(IF_ID_OP_q[25:21]),
    .STALL(hazard_detection_unit_1_stall));
  Shifter #(.width(32)) shifter_1 (.in(id_ex_1_imm_2), .\dist (5'b00010), .out(shifter_1_out));
  Multiplexer #(.select(2), .width(32)) multiplexer_2 (
    .in0(id_ex_1_data2_2), .in1(multiplexer_8_out), .in2(ex_mem_1_result_2), .out(multiplexer_2_out),
    .sel(out_1));  // open: in3
  Multiplexer #(.select(2), .width(32)) multiplexer_3 (
    .in0(id_ex_1_data1_2), .in1(multiplexer_8_out), .in2(ex_mem_1_result_2), .out(multiplexer_3_out),
    .sel(out_2));  // open: in3
  Multiplexer #(.width(32)) multiplexer_4 (
    .in0(multiplexer_2_out), .in1(id_ex_1_imm_2), .out(multiplexer_4_out), .sel(id_ex_1_alu_2[0]));
  Forwarding_unit forwarding_unit_1 (
    .EX_Mem_RegWrite(ex_mem_1_registerwriting_2), .ID_EX_RegisterRs(id_ex_1_registerrt_2),
    .ID_EX_RegisterRt(id_ex_1_registerrs_2), .EX_Mem_RegisterRd(ex_mem_1_registerrd_2),
    .EX_Mem_RegisterRt(ex_mem_1_registerrt_2), .Mem_WB_RegWrite(mipsprogramrom_1_p4),
    .Mem_WB_RegisterRd(registerfile_1_p2), .ForwardA(out_2), .ForwardB(out_1));
  Adder #(.width(32)) adder_2 (
    .a(32'h4), .b({id_ex_1_op_2_4[31:28], id_ex_1_pc_2}), .out(adder_2_out));  // open: cin, cout
  Adder #(.width(32)) adder_3 (
    .a({id_ex_1_op_2_4[31:28], id_ex_1_pc_2}), .b(shifter_1_out), .out(adder_3_out));  // open: cin, cout
  // Mips_ALU mips_alu_1: pin names not known; wires that end beside it: multiplexer_3_out, multiplexer_4_out, mips_alu_1_p3, mips_alu_1_p4, mips_alu_1_p5, id_ex_1_registerwriting_2
  ALU_control alu_control_1 (
    .ALUop(id_ex_1_alu_2[2:1]), .Output(mips_alu_1_p3), .Funct(id_ex_1_op_2_3), .IMM_OP(id_ex_1_op_2));
  and and_1 (and_1_out, or_1_out, ex_mem_1_branching_2[0]);
  Multiplexer #(.width(5)) multiplexer_5 (
    .in0(id_ex_1_op_2_4[22:18]), .in1(id_ex_1_op_2_4[17:13]), .out(multiplexer_5_out),
    .sel(id_ex_1_registerwriting_2[0]));
  EX_MEM ex_mem_1 (
    .JumpPC({id_ex_1_op_2_4, id_ex_1_op_2_3, 2'b00}), .jalPC(adder_2_out), .BranchPC(adder_3_out),
    .Zero(mips_alu_1_p4), .Result(mips_alu_1_p5), .WriteData(id_ex_1_data2_2), .Branching(id_ex_1_branch_2),
    .Memory(id_ex_1_memory_2), .RegisterWriting(id_ex_1_registerwriting_2[1]),
    .RegisterRs(id_ex_1_registerrs_2), .RegisterRt(id_ex_1_registerrt_2), .RegisterRd(multiplexer_5_out),
    .Clock(clock_1_out), .JumpPC_2(ex_mem_1_jumppc_2), .jalPC_2(ex_mem_1_jalpc_2),
    .BranchPC_2(ex_mem_1_branchpc_2), .Zero_2(ex_mem_1_zero_2), .Result_2(ex_mem_1_result_2),
    .WriteData_2(ex_mem_1_writedata_2), .Branching_2(ex_mem_1_branching_2), .Memory_2(ex_mem_1_memory_2),
    .RegisterWriting_2(ex_mem_1_registerwriting_2), .RegisterRt_2(ex_mem_1_registerrt_2),
    .RegisterRd_2(ex_mem_1_registerrd_2));  // open: NOP, RegisterRs_2
  Multiplexer #(.select(2), .width(32)) multiplexer_6 (
    .in0(ex_mem_1_jumppc_2), .in1(ex_mem_1_result_2), .in2(ex_mem_1_branchpc_2), .in3(ex_mem_1_branchpc_2),
    .out(multiplexer_6_out), .sel(ex_mem_1_branching_2[1:0]));
  or or_1 (or_1_out, ex_mem_1_branching_2[1], xor_1_out);
  xor xor_1 (xor_1_out, ex_mem_1_branching_2[2], ex_mem_1_zero_2);
  // MIPS_RAM #(.addrWidth(24)) mips_ram_1: pin names not known; wires that end beside it: ex_mem_1_branching_2, ex_mem_1_result_2[23:0], ex_mem_1_writedata_2, ex_mem_1_memory_2[1], ex_mem_1_memory_2[0], clock_1_out, mips_ram_1_p7
  MEM_WB mem_wb_1 (
    .MemoryResult(mips_ram_1_p7), .AluResult(ex_mem_1_result_2), .Branching(ex_mem_1_branching_2[3]),
    .Memory(ex_mem_1_memory_2[2]), .RegisterWriting(ex_mem_1_registerwriting_2),
    .RegisterRd(ex_mem_1_registerrd_2), .Clock(clock_1_out), .MemoryResult_2(mem_wb_1_memoryresult_2),
    .AluResult_2(mem_wb_1_aluresult_2), .Branching_2(mem_wb_1_branching_2), .Memory_2(mem_wb_1_memory_2),
    .RegisterWriting_2(mipsprogramrom_1_p4), .RegisterRd_2(registerfile_1_p2));  // open: NOP
  not not_1 (not_1_out, mem_wb_1_branching_2);
  Multiplexer #(.width(32)) multiplexer_7 (
    .in0(ex_mem_1_jalpc_2), .in1(multiplexer_8_out), .out(registerfile_1_p1), .sel(not_1_out));
  Multiplexer #(.width(32)) multiplexer_8 (
    .in0(mem_wb_1_aluresult_2), .in1(mem_wb_1_memoryresult_2), .out(multiplexer_8_out),
    .sel(mem_wb_1_memory_2));

  // Notes on the sheet:
  //   contents of mipsprogramrom_1 (hex, n*v repeats v):
  //   addiu $2, $2, 2
endmodule

module Control (
  input  [5:0] OP,
  input  [5:0] Funct,
  output SignedIMM,
  output [2:0] Alu,
  output [3:0] Branching,
  output [2:0] Memory,
  output [1:0] RegisterWriting
);

  PLA #(.in_width(6), .truth_table("001000,10#jr\n001001,11#jral")) jr_jral ();  // open: in, out
  PLA #(.in_width(8), .out_width(13), .truth_table("00000000,1100000001010#R-format\n000100xx,0000011000111#beq\n000101xx,0000011100111#bne\n001001xx,1000000001100#addiu\n001010xx,1000000001101#slti\n001100xx,1000000001100#andi\n001101xx,1000000001100#ori\n100011xx,1010100000001#lw\n101011xx,0001000000001#sw\n000010xx,0000010000000#j\n000011xx,0000010010000#jal\n00000010,0000010100000#jr\n00000011,0000010110000#jral")) pla_1 (.out(Branching));  // open: in
endmodule

module Forwarding_unit (
  input  EX_Mem_RegWrite,
  input  [4:0] ID_EX_RegisterRs,
  input  [4:0] ID_EX_RegisterRt,
  input  [4:0] EX_Mem_RegisterRd,
  input  [4:0] EX_Mem_RegisterRt,
  input  Mem_WB_RegWrite,
  input  [4:0] Mem_WB_RegisterRd,
  output [1:0] ForwardA,
  output [1:0] ForwardB
);

  wire and_1_out, and_2_out, comparator_1_eq, comparator_2_eq, comparator_3_eq, comparator_4_eq,
       comparator_5_eq, comparator_6_eq, comparator_7_eq, comparator_8_eq;

  Comparator #(.width(5), .mode("unsigned")) comparator_1 (
    .a(ID_EX_RegisterRs), .b(EX_Mem_RegisterRd), .eq(comparator_1_eq));  // open: gt, lt
  Comparator #(.width(5), .mode("unsigned")) comparator_2 (
    .a(EX_Mem_RegisterRd), .b({5{1'b0}}), .eq(comparator_2_eq));  // open: gt, lt
  Comparator #(.width(5), .mode("unsigned")) comparator_3 (
    .a(EX_Mem_RegisterRd), .b({5{1'b0}}), .eq(comparator_3_eq));  // open: gt, lt
  Comparator #(.width(5), .mode("unsigned")) comparator_4 (
    .a(ID_EX_RegisterRt), .b(EX_Mem_RegisterRt), .eq(comparator_4_eq));  // open: gt, lt
  Comparator #(.width(5), .mode("unsigned")) comparator_5 (
    .a(Mem_WB_RegisterRd), .b({5{1'b0}}), .eq(comparator_5_eq));  // open: gt, lt
  Comparator #(.width(5), .mode("unsigned")) comparator_6 (
    .a(ID_EX_RegisterRs), .b(Mem_WB_RegisterRd), .eq(comparator_6_eq));  // open: gt, lt
  Comparator #(.width(5), .mode("unsigned")) comparator_7 (
    .a(Mem_WB_RegisterRd), .b(ID_EX_RegisterRt), .eq(comparator_7_eq));  // open: gt, lt
  Comparator #(.width(5), .mode("unsigned")) comparator_8 (
    .a(EX_Mem_RegisterRd), .b(ID_EX_RegisterRt), .eq(comparator_8_eq));  // open: gt, lt
  and and_1 (and_1_out, EX_Mem_RegWrite, ~comparator_3_eq, ~comparator_6_eq);  // AND_Gate
  and and_2 (and_2_out, EX_Mem_RegWrite, ~comparator_3_eq, ~comparator_8_eq);  // AND_Gate
  and and_3 (ForwardA[1], EX_Mem_RegWrite, comparator_1_eq, ~comparator_2_eq);  // AND_Gate
  and and_4 (ForwardB[0], EX_Mem_RegWrite, comparator_3_eq, ~comparator_4_eq);  // AND_Gate
  and and_5 (ForwardA[0], Mem_WB_RegWrite, ~comparator_5_eq, ~and_1_out, comparator_6_eq);  // AND_Gate
  and and_6 (ForwardB[1], Mem_WB_RegWrite, ~comparator_5_eq, ~and_2_out, comparator_7_eq);  // AND_Gate
endmodule

module Hazard_detection_unit (
  input  ID_EX_MemRead,
  input  [4:0] ID_EX_RegisterRt,
  input  [4:0] IF_ID_RegisterRs,
  input  [4:0] IF_ID_RegisterRt,
  output STALL
);

  wire comparator_1_eq, comparator_2_eq, or_1_out;

  Comparator #(.width(5), .mode("unsigned")) comparator_1 (
    .a(ID_EX_RegisterRt), .b(IF_ID_RegisterRs), .eq(comparator_1_eq));  // open: gt, lt
  Comparator #(.width(5), .mode("unsigned")) comparator_2 (
    .a(ID_EX_RegisterRt), .b(IF_ID_RegisterRt), .eq(comparator_2_eq));  // open: gt, lt
  or or_1 (or_1_out, comparator_1_eq, comparator_2_eq);
  and and_1 (STALL, ID_EX_MemRead, or_1_out);
endmodule

module ID_EX (
  input  [31:0] PC,
  input  [31:0] Data1,
  input  [31:0] Data2,
  input  [31:0] IMM,
  input  [2:0] ALU,
  input  [3:0] Branch,
  input  [31:0] OP,
  input  [2:0] Memory,
  input  [1:0] RegisterWriting,
  input  [4:0] RegisterRs,
  input  [4:0] RegisterRt,
  input  NOP,
  input  Clock,
  output [31:0] PC_2,
  output [31:0] Data1_2,
  output [31:0] Data2_2,
  output [31:0] IMM_2,
  output [2:0] ALU_2,
  output [3:0] Branch_2,
  output [31:0] OP_2,
  output [2:0] Memory_2,
  output [1:0] RegisterWriting_2,
  output [4:0] RegisterRs_2,
  output [4:0] RegisterRt_2
);

  wire not_1_out;

  not not_1 (not_1_out, NOP);
  Register #(.width(32)) u_PC (.D(PC), .en(1'b1), .Q(PC_2), .clk(Clock));  // open: clr
  Register #(.width(32)) u_Data1 (.D(Data1), .en(1'b1), .Q(Data1_2), .clk(Clock));  // open: clr
  Register #(.width(32)) u_Data2 (.D(Data2), .en(1'b1), .Q(Data2_2), .clk(Clock));  // open: clr
  Register #(.width(32)) u_IMM (.D(IMM), .en(1'b1), .Q(IMM_2), .clk(Clock));  // open: clr
  Register #(.width(3)) u_ALU (.D(ALU), .en(not_1_out), .Q(ALU_2), .clk(Clock));  // open: clr
  Register #(.width(4)) u_Branch (.D(Branch), .en(1'b1), .Q(Branch_2), .clk(Clock));  // open: clr
  Register #(.width(32)) u_OP (.D(OP), .en(1'b1), .Q(OP_2), .clk(Clock));  // open: clr
  Register #(.width(3)) u_Memory (.D(Memory), .en(not_1_out), .Q(Memory_2), .clk(Clock));  // open: clr
  Register #(.width(2)) u_RegisterWriting (
    .D(RegisterWriting), .en(not_1_out), .Q(RegisterWriting_2), .clk(Clock));  // open: clr
  Register #(.width(5)) u_RegisterRs (.D(RegisterRs), .en(1'b1), .Q(RegisterRs_2), .clr(Clock));  // open: clk
  Register #(.width(5)) u_RegisterRt (.D(RegisterRt), .en(1'b1), .Q(RegisterRt_2), .clr(Clock));  // open: clk
endmodule

module EX_MEM (
  input  [31:0] JumpPC,
  input  [31:0] jalPC,
  input  [31:0] BranchPC,
  input  Zero,
  input  [31:0] Result,
  input  [31:0] WriteData,
  input  [3:0] Branching,
  input  [2:0] Memory,
  input  RegisterWriting,
  input  [4:0] RegisterRs,
  input  [4:0] RegisterRt,
  input  [4:0] RegisterRd,
  input  NOP,
  input  Clock,
  output [31:0] JumpPC_2,
  output [31:0] jalPC_2,
  output [31:0] BranchPC_2,
  output Zero_2,
  output [31:0] Result_2,
  output [31:0] WriteData_2,
  output [3:0] Branching_2,
  output [2:0] Memory_2,
  output RegisterWriting_2,
  output [4:0] RegisterRs_2,
  output [4:0] RegisterRt_2,
  output [4:0] RegisterRd_2
);

  // NOT_Gate not_1 has open pins: in=NOP, out=open
  Register #(.width(32)) u_JumpPC (.D(JumpPC), .en(1'b1), .Q(JumpPC_2), .clk(Clock));  // open: clr
  Register #(.width(32)) u_jalPC (.D(jalPC), .en(1'b1), .Q(jalPC_2), .clk(Clock));  // open: clr
  Register #(.width(32)) u_BranchPC (.D(BranchPC), .en(1'b1), .Q(BranchPC_2), .clk(Clock));  // open: clr
  Register #(.width(1)) u_Zero (.D(Zero), .en(1'b1), .Q(Zero_2), .clk(Clock));  // open: clr
  Register #(.width(32)) u_Result (.D(Result), .en(1'b1), .Q(Result_2), .clk(Clock));  // open: clr
  Register #(.width(32)) u_WriteData (.D(WriteData), .en(1'b1), .Q(WriteData_2), .clk(Clock));  // open: clr
  Register #(.width(4)) u_Branching (.D(Branching), .en(1'b1), .Q(Branching_2), .clk(Clock));  // open: clr
  Register #(.width(3)) u_Memory (.D(Memory), .en(1'b1), .Q(Memory_2), .clk(Clock));  // open: clr
  Register #(.width(1)) u_RegisterWriting (
    .D(RegisterWriting), .en(1'b1), .Q(RegisterWriting_2), .clk(Clock));  // open: clr
  Register #(.width(5)) u_RegisterRs (.D(RegisterRs), .en(1'b1), .Q(RegisterRs_2), .clk(Clock));  // open: clr
  Register #(.width(5)) u_RegisterRt (.D(RegisterRt), .en(1'b1), .Q(RegisterRt_2), .clk(Clock));  // open: clr
  Register #(.width(5)) u_RegisterRd (.D(RegisterRd), .en(1'b1), .Q(RegisterRd_2), .clk(Clock));  // open: clr
endmodule

module MEM_WB (
  input  [31:0] MemoryResult,
  input  [31:0] AluResult,
  input  Branching,
  input  Memory,
  input  RegisterWriting,
  input  [4:0] RegisterRd,
  input  NOP,
  input  Clock,
  output [31:0] MemoryResult_2,
  output [31:0] AluResult_2,
  output Branching_2,
  output Memory_2,
  output RegisterWriting_2,
  output [4:0] RegisterRd_2
);

  // NOT_Gate not_1 has open pins: in=NOP, out=open
  Register #(.width(32)) u_MemoryResult (.D(MemoryResult), .en(1'b1), .Q(MemoryResult_2), .clk(Clock));  // open: clr
  Register #(.width(32)) u_AluResult (.D(AluResult), .en(1'b1), .Q(AluResult_2), .clk(Clock));  // open: clr
  Register #(.width(1)) u_Branching (.D(Branching), .en(1'b1), .Q(Branching_2), .clk(Clock));  // open: clr
  Register #(.width(1)) u_Memory (.D(Memory), .en(1'b1), .Q(Memory_2), .clk(Clock));  // open: clr
  Register #(.width(1)) u_RegisterWriting (
    .D(RegisterWriting), .en(1'b1), .Q(RegisterWriting_2), .clk(Clock));  // open: clr
  Register #(.width(5)) u_RegisterRd (.D(RegisterRd), .en(1'b1), .Q(RegisterRd_2), .clk(Clock));  // open: clr
endmodule
